# Fritzing sketch version1 (saved by Fritzing 0.9.3b)
breadboards: 1

parts:
  Part1 = Arduino Uno (Rev3)
  LED1 = LED - 5mm [color="Red (633nm)" package="5 mm [THT]"]
  LED2 = LED - 5mm [color="Red (633nm)" package="5 mm [THT]"]
  LED3 = LED - 5mm [color="Red (633nm)" package="5 mm [THT]"]
  LED4 = LED - 5mm [color="Red (633nm)" package="5 mm [THT]"]
  LED5 = LED - 5mm [color="Red (633nm)" package="5 mm [THT]"]
  LED6 = LED - 5mm [color="Red (633nm)" package="5 mm [THT]"]
  LED7 = LED - 5mm [color="Red (633nm)" package="5 mm [THT]"]
  LED8 = LED - 5mm [color="Red (633nm)" package="5 mm [THT]"]
  LED9 = LED - 5mm [color="Red (633nm)" package="5 mm [THT]"]
  R1 = Resistor [tolerance=±5% resistance=470 package=THT]
  R2 = Resistor [tolerance=±5% resistance=470 package=THT]
  R3 = Resistor [tolerance=±5% resistance=470 package=THT]
  R4 = Resistor [tolerance=±5% resistance=470 package=THT]
  R5 = Resistor [tolerance=±5% resistance=470 package=THT]
  R6 = Resistor [tolerance=±5% resistance=470 package=THT]
  R7 = Resistor [tolerance=±5% resistance=470 package=THT]
  R8 = Resistor [tolerance=±5% resistance=470 package=THT]
  R9 = Resistor [tolerance=±5% resistance=470 package=THT]

nets:
  N1: Part1.D8, R7.Pin_0
  N2: Part1.D9_PWM, R9.Pin_0
  N3: Part1.D11_PWM/MOSI, R8.Pin_0
  N4: Part1.D2, R1.Pin_0
  N5: Part1.D3_PWM, R2.Pin_0
  N6: Part1.D4, R3.Pin_0
  N7: Part1.D5_PWM, R4.Pin_0
  N8: Part1.D6_PWM, R5.Pin_0
  N9: Part1.D7, R6.Pin_0
  5V: Part1.5V
  GND: Part1.GND
  N10: LED1.cathode, LED2.cathode, LED3.cathode
  N11: LED1.anode, R1.Pin_1
  N12: LED2.anode, R2.Pin_1
  N13: LED3.anode, R3.Pin_1
  N14: LED4.cathode, LED5.cathode, LED6.cathode
  N15: LED4.anode, R4.Pin_1
  N16: LED5.anode, R6.Pin_1
  N17: LED6.anode, R5.Pin_1
  N18: LED7.cathode, LED8.cathode, LED9.cathode
  N19: LED7.anode, R7.Pin_1
  N20: LED8.anode, R8.Pin_1
  N21: LED9.anode, R9.Pin_1
