# Fritzing sketch version2-board2 (saved by Fritzing 0.9.3b)
circuit board: 5.51629cm x 5.35811cm
breadboards: 1

parts:
  J3 = female pin header, 5 pins [form="♀ (female)"]
  S10 = Pushbutton [package="[THT]"]
  S11 = Pushbutton [package="[THT]"]
  S12 = Pushbutton [package="[THT]"]
  S13 = Pushbutton [package="[THT]"]
  S14 = Pushbutton [package="[THT]"]
  S15 = Pushbutton [package="[THT]"]
  S16 = Pushbutton [package="[THT]"]
  S17 = Pushbutton [package="[THT]"]
  S18 = Pushbutton [package="[THT]"]
  R30 = Resistor [tolerance=±5% resistance=4.7k package=THT]
  R31 = Resistor [tolerance=±5% resistance=4.7k package=THT]
  R32 = Resistor [tolerance=±5% resistance=4.7k package=THT]
  R33 = Resistor [tolerance=±5% resistance=2.2k package=THT]
  R34 = Resistor [tolerance=±5% resistance=2.2k package=THT]
  R35 = Resistor [tolerance=±5% resistance=10k package=THT]
  R36 = Resistor [tolerance=±5% resistance=100 package=THT]
  R37 = Resistor [tolerance=±5% resistance=2.2k package=THT]
  R38 = Resistor [tolerance=±5% resistance=10k package=THT]
  R39 = Resistor [tolerance=±5% resistance=10k package=THT]
  R40 = Resistor [tolerance=±5% resistance=100 package=THT]
  R41 = Resistor [tolerance=±5% resistance=100 package=THT]

nets:
  N1: J3.pin1, R30.Pin_0, R31.Pin_0, R32.Pin_0
  N2: J3.pin2, R33.Pin_0, R34.Pin_0, R35.Pin_1, R36.Pin_0, R37.Pin_0, R38.Pin_1, R39.Pin_1, R40.Pin_0, R41.Pin_0
  N3: J3.pin3, S10.Pin_1, S10.Pin_2, S11.Pin_1, S11.Pin_2, S12.Pin_1, S12.Pin_2, R30.Pin_1
  N4: J3.pin4, S13.Pin_1, S13.Pin_2, S14.Pin_1, S14.Pin_2, S17.Pin_1, S17.Pin_2, R31.Pin_1
  N5: J3.pin5, S15.Pin_1, S15.Pin_2, S16.Pin_1, S16.Pin_2, S18.Pin_1, S18.Pin_2, R32.Pin_1
  N6: S10.Pin_3, S10.Pin_4, R35.Pin_0
  N7: S11.Pin_3, S11.Pin_4, R40.Pin_1
  N8: S12.Pin_3, S12.Pin_4, R33.Pin_1
  N9: S13.Pin_4, R41.Pin_1
  N10: S14.Pin_4, R38.Pin_0
  N11: S15.Pin_3, S15.Pin_4, R36.Pin_1
  N12: S16.Pin_3, S16.Pin_4, R39.Pin_0
  N13: S17.Pin_3, S17.Pin_4, R37.Pin_1
  N14: S18.Pin_3, S18.Pin_4, R34.Pin_1
