# Fritzing sketch version2 (saved by Fritzing 0.9.3b)
circuit board: 10.9805cm x 6.12367cm
breadboards: 1

parts:
  R7 = Resistor [tolerance=±5% resistance=470 package=THT]
  R8 = Resistor [tolerance=±5% resistance=470 package=THT]
  R9 = Resistor [tolerance=±5% resistance=470 package=THT]
  LED1 = RGB LED (com. cathode, rgb) [package="5 mm [THT]"]
  LED2 = RGB LED (com. cathode, rgb) [package="5 mm [THT]"]
  LED3 = RGB LED (com. cathode, rgb) [package="5 mm [THT]"]
  R10 = Resistor [tolerance=±5% resistance=470 package=THT]
  LED4 = RGB LED (com. cathode, rgb) [package="5 mm [THT]"]
  LED5 = RGB LED (com. cathode, rgb) [package="5 mm [THT]"]
  LED6 = RGB LED (com. cathode, rgb) [package="5 mm [THT]"]
  R11 = Resistor [tolerance=±5% resistance=470 package=THT]
  LED7 = RGB LED (com. cathode, rgb) [package="5 mm [THT]"]
  LED8 = RGB LED (com. cathode, rgb) [package="5 mm [THT]"]
  LED9 = RGB LED (com. cathode, rgb) [package="5 mm [THT]"]
  R12 = Resistor [tolerance=±5% resistance=470 package=THT]
  R13 = Resistor [tolerance=±5% resistance=470 package=THT]
  R14 = Resistor [tolerance=±5% resistance=470 package=THT]
  R15 = Resistor [tolerance=±5% resistance=470 package=THT]
  Q1 = PNP-Transistor [package="TO92 [THT]"]
  Q2 = PNP-Transistor [package="TO92 [THT]"]
  Q3 = PNP-Transistor [package="TO92 [THT]"]
  J2 = female pin header, 1 pin [form="♀ (female)"]
  S19 = Pushbutton [package="[THT]"]
  S20 = Pushbutton [package="[THT]"]
  S21 = Pushbutton [package="[THT]"]
  S22 = Pushbutton [package="[THT]"]
  S23 = Pushbutton [package="[THT]"]
  S24 = Pushbutton [package="[THT]"]
  S25 = Pushbutton [package="[THT]"]
  S26 = Pushbutton [package="[THT]"]
  S27 = Pushbutton [package="[THT]"]
  R42 = Resistor [tolerance=±5% resistance=4.7k package=THT]
  R43 = Resistor [tolerance=±5% resistance=4.7k package=THT]
  R44 = Resistor [tolerance=±5% resistance=4.7k package=THT]
  R45 = Resistor [tolerance=±5% resistance=2.2k package=THT]
  R46 = Resistor [tolerance=±5% resistance=2.2k package=THT]
  R47 = Resistor [tolerance=±5% resistance=10k package=THT]
  R48 = Resistor [tolerance=±5% resistance=10 package=THT]
  R49 = Resistor [tolerance=±5% resistance=2.2k package=THT]
  R50 = Resistor [tolerance=±5% resistance=10k package=THT]
  R51 = Resistor [tolerance=±5% resistance=10k package=THT]
  R52 = Resistor [tolerance=±5% resistance=10 package=THT]
  R53 = Resistor [tolerance=±5% resistance=10 package=THT]
  J3 = female pin header, 1 pin [form="♀ (female)"]
  J4 = female pin header, 3 pins [form="♀ (female)"]
  J5 = female pin header, 2 pins [form="♀ (female)"]
  R55 = Resistor [tolerance=±5% resistance=1k package=THT]
  R57 = Resistor [tolerance=±5% resistance=1k package=THT]
  Part1 = Arduino Uno (Rev3)
  R56 = Resistor [tolerance=±5% resistance=1k package=THT]

nets:
  N1: R7.Pin_0, Part1.D12/MISO
  N2: R7.Pin_1, LED3.common_cathode
  N3: R8.Pin_0, Part1.D8
  N4: R8.Pin_1, LED1.common_cathode
  N5: R9.Pin_0, Part1.D9_PWM
  N6: R9.Pin_1, LED2.common_cathode
  N7: LED1.red_anode, LED2.red_anode, LED3.red_anode, LED4.red_anode, LED5.red_anode, LED6.red_anode, LED7.red_anode, LED8.red_anode, LED9.red_anode, Q3.E
  N8: LED1.green_anode, LED2.green_anode, LED3.green_anode, LED4.green_anode, LED5.green_anode, LED6.green_anode, Q2.E
  N9: LED1.blue_anode, LED2.blue_anode, LED3.blue_anode, LED4.blue_anode, LED5.blue_anode, LED6.blue_anode, LED7.blue_anode, LED8.blue_anode, LED9.blue_anode, Q1.E
  N10: R10.Pin_0, Part1.D7
  N11: R10.Pin_1, LED5.common_cathode
  N12: LED4.common_cathode, R14.Pin_1
  N13: LED6.common_cathode, R12.Pin_1
  N14: R11.Pin_0, Part1.D4
  N15: R11.Pin_1, LED8.common_cathode
  N16: LED7.common_cathode, R15.Pin_1
  N17: LED7.green_anode, LED8.green_anode, LED9.green_anode
  N18: LED9.common_cathode, R13.Pin_1
  N19: R12.Pin_0, Part1.D6_PWM
  N20: R13.Pin_0, Part1.D3_PWM
  N21: R14.Pin_0, Part1.D5_PWM
  N22: R15.Pin_0, Part1.D2
  N23: Q1.B, Part1.D11_PWM/MOSI, R56.Pin_1
  5V: Q1.C, Q2.C, Q3.C, R42.Pin_0, R43.Pin_0, R44.Pin_0, J5.pin1, Part1.5V
  N24: Q2.B, R57.Pin_1, Part1.D10_PWM/SS
  N25: Q3.B, J3.pin1, R55.Pin_1
  N26: J2.pin1, Part1.D13/SCK
  N27: S19.Pin_1, S19.Pin_2, S20.Pin_1, S20.Pin_2, S21.Pin_1, S21.Pin_2, R42.Pin_1, Part1.A3
  N28: S19.Pin_3, S19.Pin_4, R47.Pin_0
  N29: S20.Pin_3, S20.Pin_4, R52.Pin_1
  N30: S21.Pin_3, S21.Pin_4, R45.Pin_1
  N31: S22.Pin_1, S22.Pin_2, S23.Pin_1, S23.Pin_2, S26.Pin_1, S26.Pin_2, R43.Pin_1, Part1.A4/SDA
  N32: S22.Pin_4, R53.Pin_1
  N33: S23.Pin_4, R50.Pin_0
  N34: S24.Pin_1, S24.Pin_2, S25.Pin_1, S25.Pin_2, S27.Pin_1, S27.Pin_2, R44.Pin_1, Part1.A5/SCL
  N35: S24.Pin_3, S24.Pin_4, R48.Pin_1
  N36: S25.Pin_3, S25.Pin_4, R51.Pin_0
  N37: S26.Pin_3, S26.Pin_4, R49.Pin_1
  N38: S27.Pin_3, S27.Pin_4, R46.Pin_1
  GND: R45.Pin_0, R46.Pin_0, R47.Pin_1, R48.Pin_0, R49.Pin_0, R50.Pin_1, R51.Pin_1, R52.Pin_0, R53.Pin_0, J5.pin2, R55.Pin_0, R57.Pin_0, Part1.GND, R56.Pin_0
  N39: J4.pin1, Part1.A0
  N40: J4.pin2, Part1.A1
  N41: J4.pin3, Part1.A2

notes:
  E15 - B11
